// Logisim project alu.circ as structural Verilog: 1 circuit, main circuit main
module main (
  input  [31:0] X,
  input  [31:0] Y,
  input  [3:0] Switch,
  output Signed_Overflow,
  output Equal,
  output [31:0] Result,
  output [31:0] Result_2
);

  wire and_1_out, and_2_out, comparator_1_eq, comparator_2_eq, comparator_3_lt, overadd, oversub,
       subtractor_1_bout;
  wire [4:0] bit_extender_1_out, bit_extender_2_out, bit_extender_3_out;
  wire [31:0] add, addu, \and , divu, multu, \or , remainder, sll, slt, sltu, sra, srl, sub, subu, upper_mult;

  Comparator #(.width(4)) comparator_1 (.a(Switch), .b(4'b0101), .eq(comparator_1_eq));  // open: gt, lt
  Comparator #(.width(4)) comparator_2 (.a(Switch), .b(4'b0111), .eq(comparator_2_eq));  // open: gt, lt
  Bit_Extender #(.in_width(32), .out_width(5)) bit_extender_1 (.in(Y), .out(bit_extender_1_out));
  Bit_Extender #(.in_width(32), .out_width(5)) bit_extender_2 (.in(Y), .out(bit_extender_2_out));
  Bit_Extender #(.in_width(32), .out_width(5)) bit_extender_3 (.in(Y), .out(bit_extender_3_out));
  Comparator #(.width(32)) comparator_3 (.a(X), .b(Y), .lt(comparator_3_lt));  // open: gt, eq
  Subtractor #(.width(32)) subtractor_1 (.a(X), .b(Y), .bout(subtractor_1_bout));  // open: out, bin
  and and_1 (and_1_out, comparator_1_eq, overadd);
  and and_2 (and_2_out, comparator_2_eq, oversub);
  Shifter #(.width(32)) shifter_1 (.in(X), .\dist (bit_extender_1_out), .out(sll));
  Shifter #(.width(32), .shift("lr")) shifter_2 (.in(X), .\dist (bit_extender_2_out), .out(srl));
  Shifter #(.width(32), .shift("ar")) shifter_3 (.in(X), .\dist (bit_extender_3_out), .out(sra));
  assign slt = {{31{1'b0}}, comparator_3_lt};  // Bit_Extender bit_extender_4
  assign sltu = {{31{1'b0}}, subtractor_1_bout};  // Bit_Extender bit_extender_5
  or or_1 (Signed_Overflow, and_1_out, and_2_out);
  Multiplier #(.width(32)) multiplier_1 (.a(X), .b(Y), .out(multu), .cout(upper_mult));  // open: cin
  Divider #(.width(32)) divider_1 (.a(X), .b(Y), .out(divu), .rem(remainder));  // open: upper
  Adder #(.width(32)) adder_1 (.a(X), .b(Y), .out(add), .cout(overadd));  // open: cin
  Adder #(.width(32)) adder_2 (.a(X), .b(Y), .out(addu));  // open: cin, cout
  Subtractor #(.width(32)) subtractor_2 (.a(X), .b(Y), .out(sub), .bout(oversub));  // open: bin
  Subtractor #(.width(32)) subtractor_3 (.a(X), .b(Y), .out(subu));  // open: bin, bout
  assign \and  = X & Y;  // AND_Gate and_3, 32 bits wide
  assign \or  = X | Y;  // OR_Gate or_2, 32 bits wide
  Comparator #(.width(32)) comparator_4 (.a(X), .b(Y), .eq(Equal));  // open: gt, lt
  Multiplexer #(.select(4), .width(32)) multiplexer_1 (
    .in0(sll), .in1(srl), .in2(sra), .in3(multu), .in4(divu), .in5(add), .in6(addu), .in7(sub), .in8(subu),
    .in9(\and ), .in10(\or ), .in11(slt), .in12(sltu), .out(Result), .sel(Switch));  // open: in13, in14, in15, en
  Multiplexer #(.select(4), .width(32)) multiplexer_2 (
    .in0({32{1'b0}}), .in1({32{1'b0}}), .in2({32{1'b0}}), .in3(upper_mult), .in4(remainder),
    .in5({32{1'b0}}), .in6({32{1'b0}}), .in7({32{1'b0}}), .in8({32{1'b0}}), .in9({32{1'b0}}),
    .in10({32{1'b0}}), .in11({32{1'b0}}), .in12({32{1'b0}}), .out(Result_2), .sel(Switch));  // open: in13, in14, in15, en

  // Other names for the same wires on the sheet: overflow = Signed_Overflow; S[3:0] = Switch

  // Notes on the sheet:
  //   INPUTS to your circuit
  //   CHECK FOR OVERFLOW
  //   The Operations themselves
  //   DON'T CHANGE THE LOCATIONS OF THE INPUTS AND OUTPUTS!
  //   Checks whether its equal
  //   Results of resters (the MUX)
  //   OUTPUTS from your circuit
endmodule
