// Logisim project cpu.circ as structural Verilog: 3 circuits, main circuit main
module main (
  input  [31:0] INSTRUCTION,
  input  CLOCK,
  output [31:0] FETCH_ADDRESS,
  output [31:0] s0_Value,
  output [31:0] s1_Value,
  output [31:0] s2_Value,
  output [31:0] ra_Value,
  output [31:0] HI_Value,
  output [31:0] LO_Value
);

  wire ALUSRC, and_1_out, and_2_out, and_3_out, and_4_out, and_5_out, and_6_out, and_7_out, and_11_out, BEQ,
       BEQAL, BNE, branch, branchTaken, comparator_3_eq, comparator_4_eq, comparator_5_eq, comparator_6_eq,
       comparator_7_eq, comparator_9_eq, comparator_10_eq, comparator_11_eq, comparator_12_eq,
       comparator_13_eq, comparator_14_eq, eq, extop, JAL, jump, kill, lb, lbu, lhu, lui, lw, memtoreg,
       memwrite, mfhilo, multdiv, not_1_out, not_2_out, not_3_out, not_4_out, not_5_out, or_1_out, or_3_out,
       or_5_out, or_6_out, or_7_out, or_8_out, or_9_out, or_10_out, or_11_out, overflow, regDst, regWrite,
       rtype, sb, sh, shift, sw, swinc;
  wire [1:0] adder_4_out, adder_5_out, adder_7_out, adder_8_out, adder_9_out, address_type, addrselector,
       alchoosy, bit_extender_1_out, bit_extender_2_out, bit_extender_3_out, bit_extender_4_out,
       bit_extender_5_out, bit_extender_6_out, bit_extender_7_out, bit_extender_9_out, bit_extender_12_out,
       bit_extender_13_out, bit_extender_14_out, bit_extender_15_out, bit_extender_16_out, loadalu,
       multiplexer_9_out, multiplier_2_out, multiplier_3_out, multiplier_4_out, multiplier_5_out,
       multiplier_6_out, multiplier_7_out, multiplier_8_out, multiplier_10_out, multiplier_11_out,
       multiplier_12_out, regwritetype, writing_selector;
  wire [2:0] adder_12_out, adder_13_out, adder_14_out, adder_15_out, adder_16_out, adder_17_out,
       adder_18_out, bit_extender_17_out, bit_extender_18_out, bit_extender_19_out, bit_extender_20_out,
       bit_extender_21_out, bit_extender_22_out, bit_extender_23_out, bit_extender_24_out,
       bit_extender_25_out, multiplier_13_out, multiplier_14_out, multiplier_15_out, multiplier_16_out,
       multiplier_17_out, multiplier_18_out, multiplier_19_out, multiplier_20_out, multiplier_21_out, opunit;
  wire [3:0] ALUCTR;
  wire [4:0] multiplexer_5_out;
  wire [5:0] func;
  wire [7:0] bit_extender_26_out;
  wire [15:6] immediate;
  wire [31:0] adder_1_out, adder_2_out, adder_3_out, adder_20_out, bit_extender_27_out, bit_extender_28_out,
       controlled_buffer_1_out, immediate_ex, jreg, MEM_p6, multiplexer_1_out, multiplexer_2_out,
       multiplexer_3_out, multiplexer_6_out, multiplexer_8_out, multiplexer_10_out, multiplexer_11_out,
       multiplexer_12_out, multiplexer_13_out, multiplier_1_out, register2write, Ret_reg, shift_amount,
       shifter_1_out, signex, temphi, templo, zeroex;
  wire [31:16] INSTRUCTION_t;

  control_unit control_unit_1 (
    .Instruction({INSTRUCTION_t, immediate, func}), .Jump(jump), .Branch(branch), .RegDst(regDst),
    .ALUSrc(ALUSRC), .ExtOp(extop), .MemWr(memwrite), .MemtoReg(memtoreg), .RegWr(regWrite), .ALUCtr(ALUCTR),
    .JAL(JAL), .BEQAL(BEQAL), .sb(sb), .sh(sh), .sw(sw), .swinc(swinc), .lb(lb), .lbu(lbu), .lhu(lhu),
    .lw(lw), .lui(lui));
  Register #(.width(32)) PC (.D(multiplexer_2_out), .en(1'b1), .Q(FETCH_ADDRESS), .clk(CLOCK), .clr(1'b0));
  Adder #(.width(32)) adder_1 (.a(FETCH_ADDRESS), .b(signex), .out(adder_1_out));  // open: cin, cout
  Adder #(.width(32)) adder_2 (.a(adder_1_out), .b(32'h2), .out(adder_2_out));  // open: cin, cout
  Comparator #(.width(6)) comparator_1 (.a(INSTRUCTION_t[31:26]), .b(6'b000100), .eq(BEQ));  // open: gt, lt
  Comparator #(.width(6)) comparator_2 (.a(INSTRUCTION_t[31:26]), .b(6'b000101), .eq(BNE));  // open: gt, lt
  Multiplexer #(.width(32)) multiplexer_1 (
    .in0(32'h4), .in1({32{1'b0}}), .out(multiplexer_1_out), .sel(kill));  // open: en
  Subtractor #(.width(32)) subtractor_1 (.b(32'h40000));  // open: a, out, bin, bout
  Multiplier #(.width(32)) multiplier_1 (.a(adder_2_out), .b(32'h2), .out(multiplier_1_out));  // open: cin, cout
  // Probe on jreg
  not not_1 (not_1_out, eq);
  Comparator #(.width(6)) comparator_3 (.a(INSTRUCTION_t[31:26]), .b(6'b010100), .eq(comparator_3_eq));  // open: gt, lt
  Adder #(.width(32)) adder_3 (.a(FETCH_ADDRESS), .b(multiplexer_1_out), .out(adder_3_out));  // open: cin, cout
  and and_1 (and_1_out, branch, BEQ, eq);
  and and_2 (and_2_out, branch, BNE, not_1_out);
  Comparator #(.width(6)) comparator_4 (.a(func), .b(6'b001000), .eq(comparator_4_eq));  // open: gt, lt
  and and_3 (and_3_out, comparator_3_eq, eq);
  Multiplexer #(.select(2), .width(32)) multiplexer_2 (
    .in0(adder_3_out), .in1({FETCH_ADDRESS[31:28], INSTRUCTION_t[25:16], immediate, func, 2'b00}),
    .in2(multiplier_1_out), .in3(jreg), .out(multiplexer_2_out), .sel(address_type));  // open: en
  // Probe on address_type
  assign bit_extender_1_out = {{1{1'b0}}, jump};  // Bit_Extender bit_extender_1
  assign bit_extender_2_out = {{1{1'b0}}, and_1_out};  // Bit_Extender bit_extender_2
  assign bit_extender_3_out = {{1{1'b0}}, and_2_out};  // Bit_Extender bit_extender_3
  and and_4 (and_4_out, rtype, comparator_4_eq);
  assign bit_extender_4_out = {{1{1'b0}}, and_4_out};  // Bit_Extender bit_extender_4
  Multiplexer #(.width(32)) multiplexer_3 (
    .in0(INSTRUCTION), .in1({32{1'b0}}), .out(multiplexer_3_out), .sel(kill));  // open: en
  Multiplexer #(.select(2), .width(2)) multiplexer_4 (
    .in0(2'b00), .in1(2'b01), .in2(2'b10), .in3(2'b11), .out(address_type), .sel(addrselector));  // open: en
  assign bit_extender_5_out = {{1{1'b0}}, and_3_out};  // Bit_Extender bit_extender_5
  Register #(.width(32)) Pipeline (
    .D(multiplexer_3_out), .Q({INSTRUCTION_t, immediate, func}), .clk(CLOCK));  // open: en, clr
  Multiplier #(.width(2)) multiplier_2 (.a(bit_extender_1_out), .b(2'b01), .out(multiplier_2_out));  // open: cin, cout
  Multiplier #(.width(2)) multiplier_3 (.a(bit_extender_2_out), .b(2'b10), .out(multiplier_3_out));  // open: cin, cout
  Multiplier #(.width(2)) multiplier_4 (.a(bit_extender_3_out), .b(2'b10), .out(multiplier_4_out));  // open: cin, cout
  Multiplier #(.width(2)) multiplier_5 (.a(bit_extender_4_out), .b(2'b11), .out(multiplier_5_out));  // open: cin, cout
  Multiplier #(.width(2)) multiplier_6 (.a(bit_extender_5_out), .b(2'b10), .out(multiplier_6_out));  // open: cin, cout
  and and_5 (and_5_out, eq, or_1_out);
  or or_1 (or_1_out, BEQ, BEQAL);
  and and_6 (and_6_out, BNE, not_2_out);
  not not_2 (not_2_out, eq);
  // Probe on INSTRUCTION_t[31:26]
  Adder #(.width(2)) adder_4 (.a(multiplier_2_out), .b(multiplier_3_out), .out(adder_4_out));  // open: cin, cout
  Adder #(.width(2)) adder_5 (.a(multiplier_4_out), .b(multiplier_5_out), .out(adder_5_out));  // open: cin, cout
  or or_2 (branchTaken, and_5_out, and_6_out);
  Adder #(.width(2)) adder_6 (.a(adder_4_out), .b(adder_7_out), .out(addrselector));  // open: cin, cout
  Adder #(.width(2)) adder_7 (.a(adder_5_out), .b(multiplier_6_out), .out(adder_7_out));  // open: cin, cout
  not not_3 (not_3_out, JAL);
  or or_3 (or_3_out, jump, branch);
  Comparator #(.width(6)) comparator_5 (.a(INSTRUCTION_t[31:26]), .b(6'b010100), .eq(comparator_5_eq));  // open: gt, lt
  Comparator #(.width(6)) comparator_6 (.a(INSTRUCTION_t[31:26]), .b(6'b000011), .eq(comparator_6_eq));  // open: gt, lt
  // Probe on INSTRUCTION_t[31:26]
  or or_4 (kill, jump, branchTaken);
  and and_7 (and_7_out, not_3_out, or_3_out);
  assign bit_extender_6_out = {{1{1'b0}}, or_5_out};  // Bit_Extender bit_extender_6
  or or_5 (or_5_out, comparator_5_eq, comparator_6_eq);
  assign bit_extender_7_out = {{1{1'b0}}, and_7_out};  // Bit_Extender bit_extender_7
  Multiplier #(.width(2)) multiplier_7 (.a(bit_extender_6_out), .b(2'b10), .out(multiplier_7_out));  // open: cin, cout
  // Probe on INSTRUCTION_t[20:16]
  Multiplexer #(.select(2), .width(5)) multiplexer_5 (
    .in0(INSTRUCTION_t[20:16]), .in1(immediate[15:11]), .in2({5{1'b1}}), .out(multiplexer_5_out),
    .sel(regwritetype));  // open: in3, en
  // Probe on regwritetype
  // Probe on FETCH_ADDRESS
  // Probe on bit_extender_7_out
  Adder #(.width(2)) adder_8 (.a(bit_extender_7_out), .b(multiplier_7_out), .out(adder_8_out));  // open: cin, cout
  // Probe on multiplier_7_out
  assign shift_amount = {{27{1'b0}}, immediate[10:6]};  // Bit_Extender bit_extender_8
  // Probe on INSTRUCTION_t[20:16]
  // Probe on multiplexer_5_out
  Multiplexer #(.select(2), .width(32)) multiplexer_6 (
    .in0(register2write), .in1(FETCH_ADDRESS), .in2(FETCH_ADDRESS), .out(multiplexer_6_out),
    .sel(writing_selector));  // open: in3, en
  Comparator #(.width(2)) comparator_7 (.a(adder_8_out), .b(2'b11), .eq(comparator_7_eq));  // open: gt, lt
  // Probe on adder_8_out
  Comparator #(.width(6)) comparator_8 (.a(INSTRUCTION_t[31:26]), .b({6{1'b0}}), .eq(rtype));  // open: gt, lt
  assign bit_extender_9_out = {{1{1'b0}}, comparator_7_eq};  // Bit_Extender bit_extender_9
  switcher switcher_1 (.opcode(INSTRUCTION_t[31:26]), .func(func));
  assign zeroex = {{16{1'b0}}, {immediate, func}};  // Bit_Extender bit_extender_10
  assign signex = {{16{immediate[15]}}, {immediate, func}};  // Bit_Extender bit_extender_11
  or or_6 (or_6_out, BEQAL, JAL);
  regfile_main main_1 (
    .Read_Register_1(INSTRUCTION_t[25:21]), .Read_Register_2(INSTRUCTION_t[20:16]),
    .Write_Register(multiplexer_5_out), .Write_Data(multiplexer_6_out), .Write_Enable(regWrite),
    .Clock(CLOCK), .Read_Data_1(jreg), .Read_Data_2(Ret_reg), .s0_Value(s0_Value), .s1_Value(s1_Value),
    .s2_Value(s2_Value), .ra_Value(ra_Value));
  Subtractor #(.width(2)) subtractor_2 (
    .a(adder_8_out), .b(multiplier_8_out), .out(writing_selector));  // open: bin, bout
  Multiplier #(.width(2)) multiplier_8 (.a(bit_extender_9_out), .b(2'b11), .out(multiplier_8_out));  // open: cin, cout
  Multiplexer #(.width(32)) multiplexer_7 (.in0(zeroex), .in1(signex), .out(immediate_ex), .sel(extop));  // open: en
  assign bit_extender_12_out = {{1{1'b0}}, regDst};  // Bit_Extender bit_extender_12
  assign bit_extender_13_out = {{1{1'b0}}, or_6_out};  // Bit_Extender bit_extender_13
  Comparator #(.width(4)) comparator_9 (.a(ALUCTR), .b(4'b0000), .eq(comparator_9_eq));  // open: gt, lt
  Comparator #(.width(4)) comparator_10 (.a(ALUCTR), .b(4'b0001), .eq(comparator_10_eq));  // open: gt, lt
  assign bit_extender_14_out = {{1{1'b0}}, not_4_out};  // Bit_Extender bit_extender_14
  not not_4 (not_4_out, ALUSRC);
  Multiplexer #(.width(32)) multiplexer_8 (
    .in0(jreg), .in1(Ret_reg), .out(multiplexer_8_out), .sel(shift));  // open: en
  Multiplexer #(.width(2)) multiplexer_9 (
    .in0(bit_extender_14_out), .in1(2'b10), .out(multiplexer_9_out), .sel(shift));  // open: en
  Multiplier #(.width(26)) multiplier_9 (.b(26'h4));  // open: a, out, cin, cout
  Adder #(.width(2)) adder_9 (.a(bit_extender_12_out), .b(2'b00), .out(adder_9_out));  // open: cin, cout
  Multiplier #(.width(2)) multiplier_10 (
    .a(bit_extender_13_out), .b(2'b10), .out(multiplier_10_out));  // open: cin, cout
  or or_7 (or_7_out, comparator_9_eq, comparator_10_eq);
  Multiplexer #(.select(2), .width(32)) multiplexer_10 (
    .in0(immediate_ex), .in1(Ret_reg), .in2(shift_amount), .out(multiplexer_10_out), .sel(multiplexer_9_out));  // open: in3, en
  Adder #(.width(2)) adder_10 (.a(adder_9_out), .b(multiplier_10_out), .out(regwritetype));  // open: cin, cout
  // Probe on regwritetype
  and and_8 (shift, rtype, or_7_out);
  Register #(.width(32)) HI (.D(temphi), .en(multdiv), .Q(HI_Value), .clk(CLOCK), .clr(1'b0));
  or or_8 (or_8_out, lb, lbu, lw, lhu);
  Multiplexer #(.width(32)) multiplexer_11 (
    .in0(multiplexer_8_out), .in1(zeroex), .out(multiplexer_11_out), .sel(lui));  // open: en
  Multiplexer #(.select(2), .width(32)) multiplexer_12 (
    .in0(multiplexer_10_out), .in1({32{1'b0}}), .in2({32{1'b0}}), .out(multiplexer_12_out), .sel(loadalu));  // open: in3, en
  assign bit_extender_15_out = {{1{1'b0}}, lui};  // Bit_Extender bit_extender_15
  assign bit_extender_16_out = {{1{1'b0}}, or_8_out};  // Bit_Extender bit_extender_16
  // Probe on multiplexer_11_out
  // Probe on multiplexer_12_out
  Multiplier #(.width(2)) multiplier_11 (
    .a(bit_extender_15_out), .b(2'b01), .out(multiplier_11_out));  // open: cin, cout
  Multiplier #(.width(2)) multiplier_12 (
    .a(bit_extender_16_out), .b(2'b10), .out(multiplier_12_out));  // open: cin, cout
  Register #(.width(32)) LO (.D(templo), .en(multdiv), .Q(LO_Value), .clk(CLOCK), .clr(1'b0));
  alu_main main_2 (
    .Switch(ALUCTR), .X(multiplexer_11_out), .Equal(eq), .Result(temphi), .Signed_Overflow(overflow),
    .Y(multiplexer_12_out), .Result_2(templo));
  Adder #(.width(2)) adder_11 (.a(multiplier_11_out), .b(multiplier_12_out), .out(loadalu));  // open: cin, cout
  // Probe on temphi
  // Probe on opunit
  LED led_1 (.in(overflow));
  // mem_main MEM: pin names not known; wires that end beside it: temphi, Ret_reg, memwrite, CLOCK, opunit, MEM_p6
  Comparator #(.width(6)) comparator_11 (.a(func), .b(6'b011001), .eq(comparator_11_eq));  // open: gt, lt
  Comparator #(.width(6)) comparator_12 (.a(func), .b(6'b011011), .eq(comparator_12_eq));  // open: gt, lt
  Comparator #(.width(6)) comparator_13 (.a(func), .b(6'b010000), .eq(comparator_13_eq));  // open: gt, lt
  Comparator #(.width(6)) comparator_14 (.a(func), .b(6'b010010), .eq(comparator_14_eq));  // open: gt, lt
  assign bit_extender_17_out = {{2{1'b0}}, lb};  // Bit_Extender bit_extender_17
  assign bit_extender_18_out = {{2{1'b0}}, lbu};  // Bit_Extender bit_extender_18
  assign bit_extender_19_out = {{2{1'b0}}, lhu};  // Bit_Extender bit_extender_19
  assign bit_extender_20_out = {{2{1'b0}}, lw};  // Bit_Extender bit_extender_20
  assign bit_extender_21_out = {{2{1'b0}}, lui};  // Bit_Extender bit_extender_21
  assign bit_extender_22_out = {{2{1'b0}}, sb};  // Bit_Extender bit_extender_22
  assign bit_extender_23_out = {{2{1'b0}}, sh};  // Bit_Extender bit_extender_23
  assign bit_extender_24_out = {{2{1'b0}}, sw};  // Bit_Extender bit_extender_24
  assign bit_extender_25_out = {{2{1'b0}}, swinc};  // Bit_Extender bit_extender_25
  Shifter #(.width(32)) shifter_1 (.in(temphi), .\dist (5'b10000), .out(shifter_1_out));
  Multiplier #(.width(3)) multiplier_13 (
    .a(bit_extender_17_out), .b(3'b001), .out(multiplier_13_out));  // open: cin, cout
  Multiplier #(.width(3)) multiplier_14 (
    .a(bit_extender_18_out), .b(3'b000), .out(multiplier_14_out));  // open: cin, cout
  Multiplier #(.width(3)) multiplier_15 (
    .a(bit_extender_19_out), .b(3'b010), .out(multiplier_15_out));  // open: cin, cout
  Multiplier #(.width(3)) multiplier_16 (
    .a(bit_extender_20_out), .b(3'b100), .out(multiplier_16_out));  // open: cin, cout
  Multiplier #(.width(3)) multiplier_17 (
    .a(bit_extender_21_out), .b(3'b011), .out(multiplier_17_out));  // open: cin, cout
  Multiplier #(.width(3)) multiplier_18 (
    .a(bit_extender_22_out), .b(3'b000), .out(multiplier_18_out));  // open: cin, cout
  Multiplier #(.width(3)) multiplier_19 (
    .a(bit_extender_23_out), .b(3'b010), .out(multiplier_19_out));  // open: cin, cout
  Multiplier #(.width(3)) multiplier_20 (
    .a(bit_extender_24_out), .b(3'b100), .out(multiplier_20_out));  // open: cin, cout
  Multiplier #(.width(3)) multiplier_21 (
    .a(bit_extender_25_out), .b(3'b100), .out(multiplier_21_out));  // open: cin, cout
  Bit_Extender #(.in_width(32), .out_width(8)) bit_extender_26 (.in(MEM_p6), .out(bit_extender_26_out));
  // Probe on shifter_1_out
  or or_9 (or_9_out, comparator_11_eq, comparator_12_eq);
  or or_10 (or_10_out, comparator_13_eq, comparator_14_eq);
  Adder #(.width(3)) adder_12 (.a(multiplier_13_out), .b(multiplier_14_out), .out(adder_12_out));  // open: cin, cout
  Adder #(.width(3)) adder_13 (.a(multiplier_16_out), .b(multiplier_17_out), .out(adder_13_out));  // open: cin, cout
  Adder #(.width(3)) adder_14 (.a(multiplier_18_out), .b(multiplier_19_out), .out(adder_14_out));  // open: cin, cout
  Adder #(.width(3)) adder_15 (.a(multiplier_20_out), .b(multiplier_21_out), .out(adder_15_out));  // open: cin, cout
  // Probe on temphi
  assign bit_extender_27_out = {{24{1'b0}}, bit_extender_26_out};  // Bit_Extender bit_extender_27
  assign bit_extender_28_out = {{24{bit_extender_26_out[7]}}, bit_extender_26_out};  // Bit_Extender bit_extender_28
  and and_9 (multdiv, rtype, or_9_out);
  and and_10 (mfhilo, rtype, or_10_out);
  assign controlled_buffer_1_out = lw ? MEM_p6 : 32'bz;  // Controlled_Buffer controlled_buffer_1
  assign controlled_buffer_1_out = lbu ? bit_extender_27_out : 32'bz;  // Controlled_Buffer controlled_buffer_2
  assign controlled_buffer_1_out = lb ? bit_extender_28_out : 32'bz;  // Controlled_Buffer controlled_buffer_3
  assign controlled_buffer_1_out = lui ? shifter_1_out : 32'bz;  // Controlled_Buffer controlled_buffer_4
  Adder #(.width(3)) adder_16 (.a(adder_12_out), .b(multiplier_15_out), .out(adder_16_out));  // open: cin, cout
  Adder #(.width(3)) adder_17 (.a(adder_13_out), .b(adder_18_out), .out(adder_17_out));  // open: cin, cout
  Adder #(.width(3)) adder_18 (.a(adder_14_out), .b(adder_15_out), .out(adder_18_out));  // open: cin, cout
  // Probe on multiplexer_13_out
  Multiplexer #(.width(32)) multiplexer_13 (
    .in0(temphi), .in1(controlled_buffer_1_out), .out(multiplexer_13_out), .sel(memtoreg));  // open: en
  or or_11 (or_11_out, JAL, BEQAL);
  Adder #(.width(3)) adder_19 (.a(adder_16_out), .b(adder_17_out), .out(opunit));  // open: cin, cout
  Adder #(.width(32)) adder_20 (.a(FETCH_ADDRESS), .b({32{1'b0}}), .out(adder_20_out));  // open: cin, cout
  assign alchoosy = not_5_out ? 2'b00 : 2'bz;  // Controlled_Buffer controlled_buffer_5
  not not_5 (not_5_out, or_11_out);
  assign alchoosy = JAL ? 2'b01 : 2'bz;  // Controlled_Buffer controlled_buffer_6
  assign alchoosy = and_11_out ? 2'b10 : 2'bz;  // Controlled_Buffer controlled_buffer_7
  and and_11 (and_11_out, BEQAL, branchTaken);
  Multiplexer #(.select(2), .width(32)) multiplexer_14 (
    .in0(multiplexer_13_out), .in1(FETCH_ADDRESS), .in2(adder_20_out), .out(register2write), .sel(alchoosy));  // open: in3, en

  // Other names for the same wires on the sheet: clk = CLOCK; hival[31:0] = HI_Value;
  //   opcode[5:0] = INSTRUCTION_t[31:26]; immediate[5:0] = func; INSTRUCTION_t[15:0] = {immediate, func};
  //   j_address[31:2] = {FETCH_ADDRESS[31:28], INSTRUCTION_t[25:16], immediate, func};
  //   j_target[25:0] = {INSTRUCTION_t[25:16], immediate, func}; rd[4:0] = immediate[15:11];
  //   rt[4:0] = INSTRUCTION_t[20:16]; rs[4:0] = INSTRUCTION_t[25:21]; AL_val[31:0] = FETCH_ADDRESS;
  //   fetch_addr[31:0] = FETCH_ADDRESS; temp_pc[31:0] = FETCH_ADDRESS; loval[31:0] = LO_Value; raval[31:0] = ra_Value;
  //   s0val[31:0] = s0_Value; s1val[31:0] = s1_Value; s2val[31:0] = s2_Value; templui[31:0] = temphi

  // Notes on the sheet:
  //   Program Counter
  //   Control
  //   Output
  //   These are outputs/inputs from run.circ
  //   Inputs
  //   Splitter
  //   These are DEBUG/TEST outputs from your circuit.
endmodule

module control_unit (
  input  [31:0] Instruction,
  output Jump,
  output Branch,
  output RegDst,
  output ALUSrc,
  output ExtOp,
  output MemWr,
  output MemtoReg,
  output RegWr,
  output [3:0] ALUCtr,
  output JAL,
  output BEQAL,
  output sb,
  output sh,
  output sw,
  output swinc,
  output lb,
  output lbu,
  output lhu,
  output lw,
  output lui
);

  wire ADD, ADDU, AND, and_2_out, and_3_out, and_6_out, and_7_out, and_8_out, andi, beq, bne,
       comparator_1_eq, comparator_2_eq, comparator_20_eq, comparator_21_eq, comparator_22_eq,
       comparator_23_eq, comparator_24_eq, comparator_25_eq, comparator_26_eq, comparator_27_eq,
       comparator_28_eq, comparator_29_eq, comparator_30_eq, comparator_31_eq, comparator_32_eq,
       comparator_33_eq, comparator_34_eq, comparator_35_eq, DIVU, j, jr, MULTU, OR, or_1_out, or_11_out,
       ori, SLL, SLT, SLTU, SRA, SRL, SUB, SUBU;

  Comparator #(.width(6)) comparator_1 (.a(6'b000110), .b(Instruction[5:0]), .eq(comparator_1_eq));  // open: gt, lt
  Comparator #(.width(6)) comparator_2 (.a({6{1'b0}}), .b(Instruction[31:26]), .eq(comparator_2_eq));  // open: gt, lt
  Comparator #(.width(6)) comparator_3 (.a(6'b000010), .b(Instruction[31:26]), .eq(j));  // open: gt, lt
  Comparator #(.width(6)) comparator_4 (.a(6'b000011), .b(Instruction[31:26]), .eq(JAL));  // open: gt, lt
  Comparator #(.width(6)) comparator_5 (.a(6'b000100), .b(Instruction[31:26]), .eq(beq));  // open: gt, lt
  Comparator #(.width(6)) comparator_6 (.a(6'b000101), .b(Instruction[31:26]), .eq(bne));  // open: gt, lt
  Comparator #(.width(6)) comparator_7 (.a(6'b010100), .b(Instruction[31:26]), .eq(BEQAL));  // open: gt, lt
  Comparator #(.width(6)) comparator_8 (.a({6{1'b0}}), .b(Instruction[31:26]), .eq(RegDst));  // open: gt, lt
  Comparator #(.width(6)) comparator_9 (.a(6'b001100), .b(Instruction[31:26]), .eq(andi));  // open: gt, lt
  Comparator #(.width(6)) comparator_10 (.a(6'b001101), .b(Instruction[31:26]), .eq(ori));  // open: gt, lt
  Comparator #(.width(6)) comparator_11 (.a(6'b101000), .b(Instruction[31:26]), .eq(sb));  // open: gt, lt
  Comparator #(.width(6)) comparator_12 (.a(6'b101001), .b(Instruction[31:26]), .eq(sh));  // open: gt, lt
  Comparator #(.width(6)) comparator_13 (.a(6'b101011), .b(Instruction[31:26]), .eq(sw));  // open: gt, lt
  Comparator #(.width(6)) comparator_14 (.a(6'b101100), .b(Instruction[31:26]), .eq(swinc));  // open: gt, lt
  Comparator #(.width(6)) comparator_15 (.a(6'b100000), .b(Instruction[31:26]), .eq(lb));  // open: gt, lt
  Comparator #(.width(6)) comparator_16 (.a(6'b100100), .b(Instruction[31:26]), .eq(lbu));  // open: gt, lt
  Comparator #(.width(6)) comparator_17 (.a(6'b100101), .b(Instruction[31:26]), .eq(lhu));  // open: gt, lt
  Comparator #(.width(6)) comparator_18 (.a(6'b001100), .b(Instruction[31:26]), .eq(lw));  // open: gt, lt
  Comparator #(.width(6)) comparator_19 (.a(6'b001111), .b(Instruction[31:26]), .eq(lui));  // open: gt, lt
  Comparator #(.width(6)) comparator_20 (.a(6'b100000), .b(Instruction[5:0]), .eq(comparator_20_eq));  // open: gt, lt
  Comparator #(.width(6)) comparator_21 (.a(6'b001001), .b(Instruction[31:26]), .eq(comparator_21_eq));  // open: gt, lt
  Comparator #(.width(6)) comparator_22 (.a(6'b100001), .b(Instruction[5:0]), .eq(comparator_22_eq));  // open: gt, lt
  Comparator #(.width(6)) comparator_23 (.a(6'b100010), .b(Instruction[5:0]), .eq(comparator_23_eq));  // open: gt, lt
  Comparator #(.width(6)) comparator_24 (.a(6'b100011), .b(Instruction[5:0]), .eq(comparator_24_eq));  // open: gt, lt
  Comparator #(.width(6)) comparator_25 (.a(6'b100100), .b(Instruction[5:0]), .eq(comparator_25_eq));  // open: gt, lt
  Comparator #(.width(6)) comparator_26 (.a(6'b100101), .b(Instruction[5:0]), .eq(comparator_26_eq));  // open: gt, lt
  Comparator #(.width(6)) comparator_27 (.a(6'b101010), .b(Instruction[5:0]), .eq(comparator_27_eq));  // open: gt, lt
  Comparator #(.width(6)) comparator_28 (.a(6'b001010), .b(Instruction[31:26]), .eq(comparator_28_eq));  // open: gt, lt
  Comparator #(.width(6)) comparator_29 (.a(6'b101011), .b(Instruction[5:0]), .eq(comparator_29_eq));  // open: gt, lt
  Comparator #(.width(6)) comparator_30 (.a({6{1'b0}}), .b(Instruction[5:0]), .eq(comparator_30_eq));  // open: gt, lt
  Comparator #(.width(6)) comparator_31 (.a(6'b000010), .b(Instruction[5:0]), .eq(comparator_31_eq));  // open: gt, lt
  Comparator #(.width(6)) comparator_32 (.a(6'b000011), .b(Instruction[5:0]), .eq(comparator_32_eq));  // open: gt, lt
  Comparator #(.width(6)) comparator_33 (.a(6'b011001), .b(Instruction[5:0]), .eq(comparator_33_eq));  // open: gt, lt
  Comparator #(.width(6)) comparator_34 (.a(6'b011011), .b(Instruction[5:0]), .eq(comparator_34_eq));  // open: gt, lt
  and and_1 (jr, comparator_1_eq, comparator_2_eq);
  or or_1 (or_1_out, j, JAL);
  and and_2 (and_2_out, RegDst, comparator_20_eq);
  Comparator #(.width(6)) comparator_35 (.a(6'b001000), .b(Instruction[31:26]), .eq(comparator_35_eq));  // open: gt, lt
  and and_3 (and_3_out, RegDst, comparator_22_eq);
  and and_4 (SUB, comparator_23_eq, RegDst);
  and and_5 (SUBU, comparator_24_eq, RegDst);
  and and_6 (and_6_out, comparator_25_eq, RegDst);
  and and_7 (and_7_out, comparator_26_eq, RegDst);
  and and_8 (and_8_out, comparator_27_eq, RegDst);
  and and_9 (SLTU, comparator_29_eq, RegDst);
  and and_10 (SLL, comparator_30_eq, RegDst);
  and and_11 (SRL, comparator_31_eq, RegDst);
  and and_12 (SRA, comparator_32_eq, RegDst);
  and and_13 (MULTU, comparator_33_eq, RegDst);
  and and_14 (DIVU, comparator_34_eq, RegDst);
  or or_2 (Jump, jr, or_1_out);
  or or_3 (Branch, beq, bne, BEQAL);
  nor nor_1 (ALUSrc, RegDst, Jump, Branch);
  nor nor_2 (ExtOp, andi, ori);
  or or_4 (MemWr, sb, sh, sw, swinc);
  or or_5 (MemtoReg, lb, lbu, lhu, lw, lui);
  or or_6 (ADD, and_2_out, comparator_35_eq);
  or or_7 (ADDU, comparator_21_eq, and_3_out);
  or or_8 (AND, and_6_out, andi);
  or or_9 (OR, and_7_out, ori);
  or or_10 (SLT, and_8_out, comparator_28_eq);
  assign ALUCtr = or_11_out ? 4'b0000 : 4'bz;  // Controlled_Buffer controlled_buffer_1
  or or_11 (or_11_out, MemtoReg, SLL);
  assign ALUCtr = SRL ? 4'b0001 : 4'bz;  // Controlled_Buffer controlled_buffer_2
  assign ALUCtr = SRA ? 4'b0010 : 4'bz;  // Controlled_Buffer controlled_buffer_3
  assign ALUCtr = MULTU ? 4'b0011 : 4'bz;  // Controlled_Buffer controlled_buffer_4
  assign ALUCtr = DIVU ? 4'b0100 : 4'bz;  // Controlled_Buffer controlled_buffer_5
  assign ALUCtr = ADD ? 4'b0101 : 4'bz;  // Controlled_Buffer controlled_buffer_6
  assign ALUCtr = ADDU ? 4'b0110 : 4'bz;  // Controlled_Buffer controlled_buffer_7
  assign ALUCtr = SUB ? 4'b0111 : 4'bz;  // Controlled_Buffer controlled_buffer_8
  assign ALUCtr = SUBU ? 4'b1000 : 4'bz;  // Controlled_Buffer controlled_buffer_9
  assign ALUCtr = AND ? 4'b1001 : 4'bz;  // Controlled_Buffer controlled_buffer_10
  assign ALUCtr = OR ? 4'b1010 : 4'bz;  // Controlled_Buffer controlled_buffer_11
  assign ALUCtr = SLT ? 4'b1011 : 4'bz;  // Controlled_Buffer controlled_buffer_12
  assign ALUCtr = SLTU ? 4'b1100 : 4'bz;  // Controlled_Buffer controlled_buffer_13
  // OR_Gate or_12 has open pins: in3=MemWr, in5=MemtoReg, out=open
  nor nor_3 (RegWr, j, jr, beq, bne, sb, sh, sw);
  // OR_Gate or_13 has open pins: in2=Branch, out=open

  // Other names for the same wires on the sheet: address[25:0] = Instruction[25:0]; funct[5:0] = Instruction[5:0];
  //   immediate[15:0] = Instruction[15:0]; shamt[4:0] = Instruction[10:6]; rd[4:0] = Instruction[15:11];
  //   rt[4:0] = Instruction[20:16]; rs[4:0] = Instruction[25:21]; opcode[5:0] = Instruction[31:26]; Load = MemtoReg;
  //   R_type = RegDst; Store = MemWr

  // Notes on the sheet:
  //   Only the opcode and funct fields are required in this subcircuit.
  //   Feel free to paste this part into the main to get the other fields.
endmodule

module switcher (
  input  [5:0] opcode,
  input  [5:0] func
);

  wire comparator_2_eq, comparator_3_eq, itype, jtype, not_1_out, not_2_out, rtype;

  not not_1 (not_1_out, rtype);
  not not_2 (not_2_out, jtype);
  Comparator #(.width(6)) comparator_1 (.a(opcode), .b({6{1'b0}}), .eq(rtype));  // open: gt, lt
  Comparator #(.width(6)) comparator_2 (.a(opcode), .b(6'b000010), .eq(comparator_2_eq));  // open: gt, lt
  Comparator #(.width(6)) comparator_3 (.a(opcode), .b(6'b000011), .eq(comparator_3_eq));  // open: gt, lt
  and and_1 (itype, not_1_out, not_2_out);
  or or_1 (jtype, comparator_2_eq, comparator_3_eq);
endmodule
